# Fritzing sketch switch_test (saved by Fritzing 0.9.3b)
breadboards: 1

parts:
  SW1 = CD4053BCN [part_number=CD4053BCN package="DIP (Dual Inline) [THT]"]
  SW1_1 = CD4053BCN [part_number=CD4053BCN package="DIP (Dual Inline) [THT]"]  # not connected
  SW1_2 = CD4053BCN [part_number=CD4053BCN package="DIP (Dual Inline) [THT]"]  # not connected
  SW1_3 = CD4053BCN [part_number=CD4053BCN package="DIP (Dual Inline) [THT]"]  # not connected
  SW1_4 = CD4053BCN [part_number=CD4053BCN package="DIP (Dual Inline) [THT]"]  # not connected
  C1 = Ceramic Capacitor [capacitance="100 nF" package="0603 [SMD, multilayer]"]

nets:
  N1: SW1.connector0, SW1.connector15
  N2: SW1.connector1, C1.1
  N3: SW1.connector5, SW1.connector6, SW1.connector7, C1.0

notes:
  +5V from
  MSP Launchpad
  GND from
  Capacitive touchscreen
  top pad
  bottom pad
  P6.0
  22

custom parts:
  CD4053BCN: Triple 2-Channel Analog Multiplexer/Demultiplexer
  CD4053BCN: Triple 2-Channel Analog Multiplexer/Demultiplexer
  CD4053BCN: Triple 2-Channel Analog Multiplexer/Demultiplexer
  CD4053BCN: Triple 2-Channel Analog Multiplexer/Demultiplexer
  CD4053BCN: Triple 2-Channel Analog Multiplexer/Demultiplexer
