# Fritzing sketch switch_test_complete (saved by Fritzing 0.9.3b)
breadboards: 1

parts:
  SW1 = CD4053BCN [part_number=CD4053BCN package="DIP (Dual Inline) [THT]"]
  SW1_1 = CD4053BCN [part_number=CD4053BCN package="DIP (Dual Inline) [THT]"]  # not connected
  SW1_2 = CD4053BCN [part_number=CD4053BCN package="DIP (Dual Inline) [THT]"]  # not connected
  SW1_3 = CD4053BCN [part_number=CD4053BCN package="DIP (Dual Inline) [THT]"]  # not connected
  SW1_4 = CD4053BCN [part_number=CD4053BCN package="DIP (Dual Inline) [THT]"]  # not connected

nets:
  N1: SW1.connector5, SW1.connector6, SW1.connector7

notes:
  +5V from
  MSP Launchpad
  GND from
  P6.0
  o-scope probe 2
  o-scope probe 1
  +3V from
  25V Terminals of
  +2V from
  Power Supply
  GND 1 from
  GND 2 from
  6V Terminals of

custom parts:
  CD4053BCN: Triple 2-Channel Analog Multiplexer/Demultiplexer
  CD4053BCN: Triple 2-Channel Analog Multiplexer/Demultiplexer
  CD4053BCN: Triple 2-Channel Analog Multiplexer/Demultiplexer
  CD4053BCN: Triple 2-Channel Analog Multiplexer/Demultiplexer
  CD4053BCN: Triple 2-Channel Analog Multiplexer/Demultiplexer
