# Fritzing sketch touchscreen_read (saved by Fritzing 0.9.3b)
breadboards: 1

parts:
  SW1 = CD4053BCN [part_number=CD4053BCN package="DIP (Dual Inline) [THT]"]
  SW1_1 = CD4053BCN [part_number=CD4053BCN package="DIP (Dual Inline) [THT]"]  # not connected
  SW1_2 = CD4053BCN [part_number=CD4053BCN package="DIP (Dual Inline) [THT]"]  # not connected
  SW1_3 = CD4053BCN [part_number=CD4053BCN package="DIP (Dual Inline) [THT]"]  # not connected
  SW1_4 = CD4053BCN [part_number=CD4053BCN package="DIP (Dual Inline) [THT]"]  # not connected
  OA1 = LMC6482AIN Dual Op-Amp [part_number=LMC6482AIN package="DIP8 [THT]"]
  OA1_3 = LMC6482AIN Dual Op-Amp [part_number=LMC6482AIN package="DIP8 [THT]"]  # not connected
  OA1_1 = LMC6482AIN Dual Op-Amp [part_number=LMC6482AIN package="DIP8 [THT]"]  # not connected
  OA1_2 = LMC6482AIN Dual Op-Amp [part_number=LMC6482AIN package="DIP8 [THT]"]  # not connected

nets:
  N1: SW1.connector0, SW1.connector15
  N2: SW1.connector5, SW1.connector6, SW1.connector7, OA1.connector3

notes:
  +5V from
  MSP Launchpad
  GND from
  All sources share same GND
  +12V from
  Power Supply Unit
  GNDs from 6V and 12V
  +6V from
  THIS BREADBOARD
  IS NOT COMPLETE

custom parts:
  CD4053BCN: Triple 2-Channel Analog Multiplexer/Demultiplexer
  CD4053BCN: Triple 2-Channel Analog Multiplexer/Demultiplexer
  CD4053BCN: Triple 2-Channel Analog Multiplexer/Demultiplexer
  CD4053BCN: Triple 2-Channel Analog Multiplexer/Demultiplexer
  CD4053BCN: Triple 2-Channel Analog Multiplexer/Demultiplexer
  LMC6482AIN Dual Op-Amp: Dual Rail-to-Rail Input and Output Operational Amplifier
  LMC6482AIN Dual Op-Amp: Dual Rail-to-Rail Input and Output Operational Amplifier
  LMC6482AIN Dual Op-Amp: Dual Rail-to-Rail Input and Output Operational Amplifier
  LMC6482AIN Dual Op-Amp: Dual Rail-to-Rail Input and Output Operational Amplifier
